// Logisim project hw3.circ as structural Verilog
module _1_BitFullAdder (
  input  A,
  input  B,
  input  CarryIn,
  output Carry_Out,
  output Answer
);

  wire and_1_out, and_2_out, and_3_out, and_4_out, and_5_out, and_6_out, and_7_out, not_1_out, not_2_out,
       not_3_out, not_4_out, not_5_out, not_6_out, not_7_out, not_8_out, not_9_out;

  not not_1 (not_1_out, A);
  not not_2 (not_2_out, B);
  and and_1 (and_1_out, not_1_out, not_2_out, CarryIn);
  not not_3 (not_3_out, A);
  and and_2 (and_2_out, not_3_out, B, not_4_out);
  not not_4 (not_4_out, CarryIn);
  not not_5 (not_5_out, A);
  and and_3 (and_3_out, not_5_out, B, CarryIn);
  not not_6 (not_6_out, B);
  and and_4 (and_4_out, A, not_6_out, not_7_out);
  not not_7 (not_7_out, CarryIn);
  and and_5 (and_5_out, A, not_8_out, CarryIn);
  not not_8 (not_8_out, B);
  and and_6 (and_6_out, A, B, not_9_out);
  not not_9 (not_9_out, CarryIn);
  and and_7 (and_7_out, A, B, CarryIn);
  or or_1 (Carry_Out, and_3_out, and_5_out, and_6_out, and_7_out);
  or or_2 (Answer, and_7_out, and_1_out, and_2_out, and_4_out);
endmodule

module _4_BitFullAdder (
  input  [3:0] B,
  input  [3:0] A,
  input  Carry_In,
  output Carry_Out,
  output [3:0] Answer
);

  wire n1_bitfulladder_2_carry_out, n1_bitfulladder_3_carry_out, n1_bitfulladder_4_carry_out;

  _1_BitFullAdder u_1_bitfulladder_1 (
    .A(A[3]), .B(B[3]), .CarryIn(n1_bitfulladder_2_carry_out), .Carry_Out(Carry_Out), .Answer(Answer[3]));
  _1_BitFullAdder u_1_bitfulladder_2 (
    .A(A[2]), .B(B[2]), .CarryIn(n1_bitfulladder_3_carry_out), .Carry_Out(n1_bitfulladder_2_carry_out),
    .Answer(Answer[2]));
  _1_BitFullAdder u_1_bitfulladder_3 (
    .A(A[1]), .B(B[1]), .CarryIn(n1_bitfulladder_4_carry_out), .Carry_Out(n1_bitfulladder_3_carry_out),
    .Answer(Answer[1]));
  _1_BitFullAdder u_1_bitfulladder_4 (
    .A(A[0]), .B(B[0]), .CarryIn(Carry_In), .Carry_Out(n1_bitfulladder_4_carry_out), .Answer(Answer[0]));

  // Other names for the same wires on the sheet: Output_0 = Answer[0]; Output_1 = Answer[1]; Output_2 = Answer[2];
  //   Output_3 = Answer[3]
endmodule

module _4_BitALU (
  input  in_1,
  input  Selectors,
  input  in_3,
  input  [3:0] Input_A,
  input  [3:0] Input_B,
  output [3:0] Answer
);

  wire [0:0] and_1_out;
  wire [3:0] n4_bitfulladder_1_answer, n4_bitfulladder_2_answer, n4_bitfulladder_3_answer, nand_1_out,
       nor_1_out, not_1_out, not_2_out, xor_1_out;

  assign not_1_out = ~Input_B;  // NOT_Gate not_1, 4 bits wide
  _4_BitFullAdder u_4_bitfulladder_1 (
    .B(Input_A), .A(Input_B), .Carry_In(1'b0), .Answer(n4_bitfulladder_1_answer));  // open: Carry_Out
  _4_BitFullAdder u_4_bitfulladder_2 (
    .B(Input_A), .A(not_1_out), .Carry_In(1'b1), .Answer(n4_bitfulladder_2_answer));  // open: Carry_Out
  assign not_2_out = ~Input_A;  // NOT_Gate not_2, 4 bits wide
  _4_BitFullAdder u_4_bitfulladder_3 (
    .B(not_2_out), .A(4'b0000), .Carry_In(1'b1), .Answer(n4_bitfulladder_3_answer));  // open: Carry_Out
  assign nand_1_out = ~(Input_A & Input_B);  // NAND_Gate nand_1, 4 bits wide
  assign nor_1_out = ~(Input_A | Input_B);  // NOR_Gate nor_1, 4 bits wide
  assign xor_1_out = Input_A ^ Input_B;  // XOR_Gate xor_1, 4 bits wide
  and and_1 (and_1_out[0], ~Input_A[0], ~Input_A[1]);  // AND_Gate
  Multiplexer #(.select(3), .width(4), .disabled(0), .enable("false")) multiplexer_1 (
    .in0(n4_bitfulladder_1_answer), .in1(n4_bitfulladder_2_answer), .in2({3'b000, and_1_out[0]}),
    .in3(n4_bitfulladder_3_answer), .in4({Input_A[2:0], 1'b0}), .in5(nand_1_out), .in6(nor_1_out),
    .in7(xor_1_out), .out(Answer), .sel({in_1, Selectors, in_3}));

  // Other names for the same wires on the sheet: A[3:0] = Input_A; S0 = in_3; S1 = Selectors; S2 = in_1;
  //   B[3:0] = Input_B

  // Notes on the sheet:
  //   Op-Codes
  //   S0 S1 S2 Function
  //   0 0 0 Addition
  //   0 0 1 Subtraction
  //   0 1 0 isMultipleOf4
  //   0 1 1 TwosComplement
  //   1 0 0 Multiply By 2
  //   1 0 1 NAND
  //   1 1 0 NOR
  //   1 1 1 XOR
endmodule

module _16_BitAdder (
  input  [15:0] A,
  input  [15:0] B,
  input  in_3,
  output [15:0] Output
);

  wire Carry_Out_0, Carry_Out_1, Carry_Out_2, Carry_Out_3;

  _4_BitFullAdder u_4_bitfulladder_1 (
    .B(A[11:8]), .A(B[11:8]), .Carry_In(Carry_Out_1), .Carry_Out(Carry_Out_2), .Answer(Output[11:8]));
  _4_BitFullAdder u_4_bitfulladder_2 (
    .B(A[15:12]), .A(B[15:12]), .Carry_In(Carry_Out_2), .Carry_Out(Carry_Out_3), .Answer(Output[15:12]));
  _4_BitFullAdder u_4_bitfulladder_3 (
    .B(A[7:4]), .A(B[7:4]), .Carry_In(Carry_Out_0), .Carry_Out(Carry_Out_1), .Answer(Output[7:4]));
  _4_BitFullAdder u_4_bitfulladder_4 (
    .B(A[3:0]), .A(B[3:0]), .Carry_In(in_3), .Carry_Out(Carry_Out_0), .Answer(Output[3:0]));

  // Other names for the same wires on the sheet: A0[3:0] = A[3:0]; A1[3:0] = A[7:4]; A2[3:0] = A[11:8];
  //   A3[3:0] = A[15:12]; B0[3:0] = B[3:0]; B1[3:0] = B[7:4]; B2[3:0] = B[11:8]; B3[3:0] = B[15:12]; Carry_In = in_3;
  //   Output_0[3:0] = Output[3:0]; Output_1[3:0] = Output[7:4]; Output_2[3:0] = Output[11:8];
  //   Output_3[3:0] = Output[15:12]
endmodule

module _16_BitALU (
  input  in_1,
  input  in_2,
  input  in_3,
  input  [15:0] A,
  input  [15:0] B,
  output [15:0] Output
);

  wire [0:0] and_1_out;
  wire [15:0] n16_bitadder_1_output, n16_bitadder_2_output, n16_bitadder_3_output, nand_1_out, nor_1_out,
       not_1_out, not_2_out, xor_1_out;

  _16_BitAdder u_16_bitadder_1 (.A(A), .B(B), .in_3(1'b0), .Output(n16_bitadder_1_output));
  assign not_1_out = ~B;  // NOT_Gate not_1, 16 bits wide
  _16_BitAdder u_16_bitadder_2 (.A(A), .B(not_1_out), .in_3(1'b1), .Output(n16_bitadder_2_output));
  assign not_2_out = ~A;  // NOT_Gate not_2, 16 bits wide
  _16_BitAdder u_16_bitadder_3 (.A(not_2_out), .B({16{1'b0}}), .in_3(1'b1), .Output(n16_bitadder_3_output));
  assign nand_1_out = ~(A & B);  // NAND_Gate nand_1, 16 bits wide
  and and_1 (and_1_out[0], ~A[0], ~A[1]);  // AND_Gate
  assign nor_1_out = ~(A | B);  // NOR_Gate nor_1, 16 bits wide
  assign xor_1_out = A ^ B;  // XOR_Gate xor_1, 16 bits wide
  Multiplexer #(.select(3), .width(16), .disabled(0), .enable("false")) multiplexer_1 (
    .in0(n16_bitadder_1_output), .in1(n16_bitadder_2_output), .in2({{15{1'b0}}, and_1_out[0]}),
    .in3(n16_bitadder_3_output), .in4({A[12:0], 3'b000}), .in5(nand_1_out), .in6(nor_1_out), .in7(xor_1_out),
    .out(Output), .sel({in_1, in_2, in_3}));

  // Other names for the same wires on the sheet: S0 = in_3; S1 = in_2; S2 = in_1

  // Notes on the sheet:
  //   S0 S1 S2 Function
  //   0 0 0 Addition
  //   0 0 1 Subtraction
  //   0 1 0 isMultipleOf4
  //   0 1 1 TwosComplement
  //   1 0 0 Multiply By 8
  //   1 0 1 NAND
  //   1 1 0 NOR
  //   1 1 1 XOR
endmodule
